// Digital circuit 4Bit_Ram_Module.dig as structural Verilog
module _4Bit_Ram_Module (
  input  Read_Write,
  input  [3:0] MemAddress,
  input  [3:0] Data,
  input  setClear,
  input  setLoad,
  output [3:0] Dout
);

  wire and_1_out, and_2_out, and_3_out, and_4_out, and_5_out, and_6_out, and_7_out, and_8_out, and_9_out,
       and_10_out, and_11_out, and_12_out, and_13_out, and_14_out, and_15_out, and_16_out, decoder_1_out_0,
       decoder_1_out_1, decoder_1_out_2, decoder_1_out_3, decoder_1_out_4, decoder_1_out_5, decoder_1_out_6,
       decoder_1_out_7, decoder_1_out_8, decoder_1_out_9, decoder_1_out_10, decoder_1_out_11,
       decoder_1_out_12, decoder_1_out_13, decoder_1_out_14, decoder_1_out_15;
  wire [3:0] _0_q, _1_q, _2_q, _3_q, _4_q, _5_q, _6_q, _7_q, _8_q, _9_q, _10_q, _11_q, _12_q, _13_q, _14_q,
       _15_q;

  Decoder #(.Selector_Bits(4)) decoder_1 (
    .sel(MemAddress), .out_0(decoder_1_out_0), .out_1(decoder_1_out_1), .out_2(decoder_1_out_2),
    .out_3(decoder_1_out_3), .out_4(decoder_1_out_4), .out_5(decoder_1_out_5), .out_6(decoder_1_out_6),
    .out_7(decoder_1_out_7), .out_8(decoder_1_out_8), .out_9(decoder_1_out_9), .out_10(decoder_1_out_10),
    .out_11(decoder_1_out_11), .out_12(decoder_1_out_12), .out_13(decoder_1_out_13),
    .out_14(decoder_1_out_14), .out_15(decoder_1_out_15));
  and and_1 (and_1_out, decoder_1_out_0, Read_Write);
  and and_2 (and_2_out, decoder_1_out_1, Read_Write);
  and and_3 (and_3_out, decoder_1_out_2, Read_Write);
  and and_4 (and_4_out, decoder_1_out_3, Read_Write);
  and and_5 (and_5_out, decoder_1_out_4, Read_Write);
  and and_6 (and_6_out, decoder_1_out_5, Read_Write);
  and and_7 (and_7_out, decoder_1_out_6, Read_Write);
  and and_8 (and_8_out, decoder_1_out_7, Read_Write);
  and and_9 (and_9_out, decoder_1_out_8, Read_Write);
  and and_10 (and_10_out, decoder_1_out_9, Read_Write);
  and and_11 (and_11_out, decoder_1_out_10, Read_Write);
  and and_12 (and_12_out, decoder_1_out_11, Read_Write);
  and and_13 (and_13_out, decoder_1_out_12, Read_Write);
  and and_14 (and_14_out, decoder_1_out_13, Read_Write);
  and and_15 (and_15_out, decoder_1_out_14, Read_Write);
  and and_16 (and_16_out, decoder_1_out_15, Read_Write);
  _4bit_register _0 (.In(Data), .Clock(and_1_out), .setClear(setClear), .setLoad(setLoad), .Q(_0_q));  // open: Q_2
  _4bit_register _1 (.In(Data), .Clock(and_2_out), .setClear(setClear), .setLoad(setLoad), .Q(_1_q));  // open: Q_2
  _4bit_register _2 (.In(Data), .Clock(and_3_out), .setClear(setClear), .setLoad(setLoad), .Q(_2_q));  // open: Q_2
  _4bit_register _3 (.In(Data), .Clock(and_4_out), .setClear(setClear), .setLoad(setLoad), .Q(_3_q));  // open: Q_2
  _4bit_register _4 (.In(Data), .Clock(and_5_out), .setClear(setClear), .setLoad(setLoad), .Q(_4_q));  // open: Q_2
  _4bit_register _5 (.In(Data), .Clock(and_6_out), .setClear(setClear), .setLoad(setLoad), .Q(_5_q));  // open: Q_2
  _4bit_register _6 (.In(Data), .Clock(and_7_out), .setClear(setClear), .setLoad(setLoad), .Q(_6_q));  // open: Q_2
  _4bit_register _7 (.In(Data), .Clock(and_8_out), .setClear(setClear), .setLoad(setLoad), .Q(_7_q));  // open: Q_2
  _4bit_register _8 (.In(Data), .Clock(and_9_out), .setClear(setClear), .setLoad(setLoad), .Q(_8_q));  // open: Q_2
  _4bit_register _9 (.In(Data), .Clock(and_10_out), .setClear(setClear), .setLoad(setLoad), .Q(_9_q));  // open: Q_2
  _4bit_register _10 (.In(Data), .Clock(and_11_out), .setClear(setClear), .setLoad(setLoad), .Q(_10_q));  // open: Q_2
  _4bit_register _11 (.In(Data), .Clock(and_12_out), .setClear(setClear), .setLoad(setLoad), .Q(_11_q));  // open: Q_2
  _4bit_register _12 (.In(Data), .Clock(and_13_out), .setClear(setClear), .setLoad(setLoad), .Q(_12_q));  // open: Q_2
  _4bit_register _13 (.In(Data), .Clock(and_14_out), .setClear(setClear), .setLoad(setLoad), .Q(_13_q));  // open: Q_2
  _4bit_register _14 (.In(Data), .Clock(and_15_out), .setClear(setClear), .setLoad(setLoad), .Q(_14_q));  // open: Q_2
  _4bit_register _15 (.In(Data), .Clock(and_16_out), .setClear(setClear), .setLoad(setLoad), .Q(_15_q));  // open: Q_2
  Multiplexer #(.Selector_Bits(4), .Bits(4)) multiplexer_1 (
    .sel(MemAddress), .in_0(_0_q), .in_1(_1_q), .in_2(_2_q), .in_3(_3_q), .in_4(_4_q), .in_5(_5_q),
    .in_6(_6_q), .in_7(_7_q), .in_8(_8_q), .in_9(_9_q), .in_10(_10_q), .in_11(_11_q), .in_12(_12_q),
    .in_13(_13_q), .in_14(_14_q), .in_15(_15_q), .out(Dout));
endmodule
