// Digital circuit 4bit_ALU.dig as structural Verilog
module _4bit_ALU (
  input  [3:0] A,
  input  [3:0] B,
  input  [2:0] Control,
  output [3:0] Output,
  output Zero_Flag
);

  wire [0:0] slt_1_p3;
  wire [3:0] _4bit_adder_1_p4, _4bit_adder_subractor_1_p4, and_1_out, or_1_out, xor_1_out;

  // _4bit_adder _4bit_adder_1: pin names not known; wires that end beside it: 1'b0, A, B, _4bit_adder_1_p4
  // _4bit_adder_subractor _4bit_adder_subractor_1: pin names not known; wires that end beside it: 1'b1, A, B, _4bit_adder_subractor_1_p4
  assign and_1_out = A & B;  // And and_1, 4 bits wide
  assign or_1_out = A | B;  // Or or_1, 4 bits wide
  assign xor_1_out = A ^ B;  // XOr xor_1, 4 bits wide
  // SLT slt_1: pin names not known; wires that end beside it: A, B, slt_1_p3[0]
  Multiplexer #(.Selector_Bits(3), .Bits(4)) multiplexer_1 (
    .sel(Control), .in_0(_4bit_adder_1_p4), .in_1(_4bit_adder_subractor_1_p4), .in_2(and_1_out),
    .in_3(or_1_out), .in_4(xor_1_out), .in_5({3'b000, slt_1_p3[0]}), .in_6(A), .in_7(B), .out(Output));
  nor nor_1 (Zero_Flag, Output[0], Output[1], Output[2], Output[3]);
endmodule
