// Digital circuit 4bit_CPU.dig as structural Verilog
module _4bit_CPU (
  input  [3:0] NxtMemAdrs,
  input  SysFlush,
  input  PC_CTRL,
  input  PC_Freeze,
  input  PC_Clr,
  input  [3:0] A_in,
  input  A_CTRL,
  input  A_Freeze,
  input  A_Clr,
  input  [3:0] B_in,
  input  B_Freeze,
  input  B_Clr,
  input  IR_Freeze,
  input  IR_Clr,
  input  Clock,
  output [3:0] Output,
  output Z_Flag
);

  wire or_1_out, or_2_out, or_3_out, or_4_out;
  wire [3:0] A_q, B_q, IR_q, multiplexer_1_out, PC_output;

  Multiplexer #(.Bits(4)) multiplexer_1 (.sel(A_CTRL), .in_0(A_in), .in_1(Output), .out(multiplexer_1_out));
  or or_1 (or_1_out, SysFlush, PC_Clr);
  or or_2 (or_2_out, SysFlush, A_Clr);
  or or_3 (or_3_out, SysFlush, B_Clr);
  or or_4 (or_4_out, SysFlush, IR_Clr);
  _4bit_PC PC (
    .PC_IN(NxtMemAdrs), .Control(PC_CTRL), .Clock(Clock), .setClear(or_1_out), .setLoad(PC_Freeze),
    .Output(PC_output));
  _4bit_register A (
    .In(multiplexer_1_out), .Clock(Clock), .setClear(or_2_out), .setLoad(A_Freeze), .Q(A_q));  // open: Q_2
  _4bit_register B (.In(B_in), .Clock(Clock), .setClear(or_3_out), .setLoad(B_Freeze), .Q(B_q));  // open: Q_2
  _4bit_register IR (.In(PC_output), .Clock(Clock), .setClear(or_4_out), .setLoad(IR_Freeze), .Q(IR_q));  // open: Q_2
  _4bit_ALU _4bit_alu_1 (.A(A_q), .B(B_q), .Control(IR_q[2:0]), .Output(Output), .Zero_Flag(Z_Flag));
endmodule
