// Digital circuit 4bit_PC.dig as structural Verilog
module _4bit_PC (
  input  [3:0] PC_IN,
  input  Control,
  input  Clock,
  input  setClear,
  input  setLoad,
  output [3:0] Output
);

  wire [3:0] _4bit_adder_1_p4, multiplexer_1_out;

  Multiplexer #(.Bits(4)) multiplexer_1 (.sel(Control), .in_0(PC_IN), .in_1(_4bit_adder_1_p4), .out(multiplexer_1_out));
  _4bit_register _4bit_register_1 (
    .In(multiplexer_1_out), .Clock(Clock), .setClear(setClear), .setLoad(setLoad), .Q(Output));  // open: Q_2
  // _4bit_adder _4bit_adder_1: pin names not known; wires that end beside it: 1'b0, Output, 4'b0001, _4bit_adder_1_p4
endmodule
