// Digital circuit 4bit_register.dig as structural Verilog
module _4bit_register (
  input  [3:0] In,
  input  Clock,
  input  setClear,
  input  setLoad,
  output [3:0] Q,
  output [3:0] Q_2
);

  wire and_1_out, multiplexer_1_out, multiplexer_2_out, multiplexer_3_out, multiplexer_4_out,
       multiplexer_5_out, multiplexer_6_out, multiplexer_7_out, multiplexer_8_out, not_1_out;

  not not_1 (not_1_out, setClear);
  and and_1 (and_1_out, not_1_out, setLoad);
  Multiplexer multiplexer_1 (.sel(setClear), .in_0(In[0]), .in_1(1'b0), .out(multiplexer_1_out));
  D_FF _2_0 (.D(multiplexer_3_out), .C(Clock), .Q(Q[0]), .nQ(Q_2[0]));
  Multiplexer multiplexer_2 (.sel(setClear), .in_0(In[1]), .in_1(1'b0), .out(multiplexer_2_out));
  Multiplexer multiplexer_3 (.sel(and_1_out), .in_0(multiplexer_1_out), .in_1(Q[0]), .out(multiplexer_3_out));
  Multiplexer multiplexer_4 (.sel(and_1_out), .in_0(multiplexer_2_out), .in_1(Q[1]), .out(multiplexer_4_out));
  D_FF _2_1 (.D(multiplexer_4_out), .C(Clock), .Q(Q[1]), .nQ(Q_2[1]));
  Multiplexer multiplexer_5 (.sel(setClear), .in_0(In[2]), .in_1(1'b0), .out(multiplexer_5_out));
  Multiplexer multiplexer_6 (.sel(and_1_out), .in_0(multiplexer_5_out), .in_1(Q[2]), .out(multiplexer_6_out));
  D_FF _2_2 (.D(multiplexer_6_out), .C(Clock), .Q(Q[2]), .nQ(Q_2[2]));
  Multiplexer multiplexer_7 (.sel(setClear), .in_0(In[3]), .in_1(1'b0), .out(multiplexer_7_out));
  D_FF _2_3 (.D(multiplexer_8_out), .C(Clock), .Q(Q[3]), .nQ(Q_2[3]));
  Multiplexer multiplexer_8 (.sel(and_1_out), .in_0(multiplexer_7_out), .in_1(Q[3]), .out(multiplexer_8_out));
endmodule
